# Fritzing sketch day5 (saved by Fritzing 0.9.4)
breadboards: 1

parts:
  R1 = Resistor [tolerance=±5% resistance=1k package=THT]
  U1 = POT [package=3362u]
  Bela1 = Bela
  U2 = POT [package=3362u]
  R2 = Resistor [tolerance=±5% resistance=220 package=THT]

nets:
  N1: R1.Pin_0, Bela1.AOUT_5V, R2.Pin_0
  N2: R1.Pin_1, U1.A
  N3: U1.E, Bela1.AOUT_GND, U2.E
  N4: U1.S, Bela1.AIN_0
  N5: Bela1.AIN_1, U2.S
  N6: U2.A, R2.Pin_1

custom parts:
  Bela: A Fritzing part for Bela
