# Fritzing sketch p3 (saved by Fritzing 0.9.4)
breadboards: 1

parts:
  Bela1 = Bela
  U1 = POT [package=3362u]
  U2 = POT [package=3362u]
  U3 = POT [package=3362u]
  U4 = POT [package=3362u]
  S1 = Pushbutton [package="[SMD]"]
  J1 = Piezo Speaker  # not connected
  J2 = Piezo Speaker  # not connected

nets:
  N1: Bela1.P8_01_GND, U3.E, U4.E
  N2: Bela1.P8_02_GND, U3.A, U4.A
  N3: Bela1.P8_07_D0, S1.Pin_1, S1.Pin_2
  N4: Bela1.P9_03_3.3V, S1.Pin_3, S1.Pin_4
  N5: Bela1.AIN_3, U2.S
  N6: Bela1.AIN_2, U1.S
  N7: Bela1.AIN_1, U4.S
  N8: Bela1.AIN_0, U3.S
  N9: U1.E, U2.E
  N10: U1.A, U2.A

custom parts:
  Bela: A Fritzing part for Bela
